# Fritzing sketch dactylize2 (saved by Fritzing 0.9.2b)
circuit board: 8.46667cm x 5.64444cm
breadboards: 2
stripboards: 1

parts:
  U1 = 74HC165 [part_number=SN74LS165 package="DIP16 [THT]"]
  U2 = 74HC165 [part_number=SN74LS165 package="DIP16 [THT]"]
  U3 = 74HC165 [part_number=SN74LS165 package="DIP16 [THT]"]
  U4 = 74HC165 [part_number=SN74LS165 package="DIP16 [THT]"]
  U5 = 74HC165 [part_number=SN74LS165 package="DIP16 [THT]"]
  U6 = 74HC165 [part_number=SN74LS165 package="DIP16 [THT]"]
  J2 = double row male pin header, 4 pins [form="♂ (male)"]
  J3 = double row male pin header, 4 pins [form="♂ (male)"]
  J4 = double row male pin header, 4 pins [form="♂ (male)"]
  J5 = double row male pin header, 4 pins [form="♂ (male)"]
  J6 = double row male pin header, 4 pins [form="♂ (male)"]
  J7 = double row male pin header, 4 pins [form="♂ (male)"]
  J8 = double row male pin header, 4 pins [form="♂ (male)"]
  J9 = double row male pin header, 4 pins [form="♂ (male)"]
  J10 = double row male pin header, 4 pins [form="♂ (male)"]
  J11 = double row male pin header, 4 pins [form="♂ (male)"]
  J12 = double row male pin header, 4 pins [form="♂ (male)"]
  Part1 = Arduino Uno (Rev3)
  J13 = double row male pin header, 4 pins [form="♂ (male)"]
  R1 = Resistor [tolerance=±5% resistance=10k package=THT]
  C1 = Ceramic Capacitor [capacitance=100nF package="100 mil [THT, multilayer]"]
  C2 = Ceramic Capacitor [capacitance=100nF package="100 mil [THT, multilayer]"]
  R2 = Resistor [tolerance=±5% resistance=10k package=THT]
  R3 = Resistor [tolerance=±5% resistance=10k package=THT]
  R4 = Resistor [tolerance=±5% resistance=10k package=THT]
  R6 = Resistor [tolerance=±5% resistance=10k package=THT]
  R7 = Resistor [tolerance=±5% resistance=10k package=THT]
  R9 = Resistor [tolerance=±5% resistance=10k package=THT]
  R10 = Resistor [tolerance=±5% resistance=10k package=THT]
  R11 = Resistor [tolerance=±5% resistance=10k package=THT]
  R12 = Resistor [tolerance=±5% resistance=10k package=THT]
  R13 = Resistor [tolerance=±5% resistance=10k package=THT]
  R14 = Resistor [tolerance=±5% resistance=10k package=THT]
  R15 = Resistor [tolerance=±5% resistance=10k package=THT]
  R16 = Resistor [tolerance=±5% resistance=10k package=THT]
  R17 = Resistor [tolerance=±5% resistance=10k package=THT]
  R18 = Resistor [tolerance=±5% resistance=10k package=THT]
  R19 = Resistor [tolerance=±5% resistance=10k package=THT]
  R20 = Resistor [tolerance=±5% resistance=10k package=THT]
  R21 = Resistor [tolerance=±5% resistance=10k package=THT]
  R22 = Resistor [tolerance=±5% resistance=10k package=THT]
  R23 = Resistor [tolerance=±5% resistance=10k package=THT]
  R24 = Resistor [tolerance=±5% resistance=10k package=THT]
  R25 = Resistor [tolerance=±5% resistance=10k package=THT]
  R26 = Resistor [tolerance=±5% resistance=10k package=THT]
  R27 = Resistor [tolerance=±5% resistance=10k package=THT]
  R28 = Resistor [tolerance=±5% resistance=10k package=THT]
  R29 = Resistor [tolerance=±5% resistance=10k package=THT]
  R30 = Resistor [tolerance=±5% resistance=10k package=THT]
  C3 = Ceramic Capacitor [capacitance=100nF package="100 mil [THT, multilayer]"]
  C4 = Ceramic Capacitor [capacitance=100nF package="100 mil [THT, multilayer]"]
  C5 = Ceramic Capacitor [capacitance=100nF package="100 mil [THT, multilayer]"]
  R31 = Resistor [tolerance=±5% resistance=10k package=THT]
  R32 = Resistor [tolerance=±5% resistance=10k package=THT]
  R33 = Resistor [tolerance=±5% resistance=10k package=THT]
  R34 = Resistor [tolerance=±5% resistance=10k package=THT]
  R35 = Resistor [tolerance=±5% resistance=10k package=THT]
  R36 = Resistor [tolerance=±5% resistance=10k package=THT]
  R37 = Resistor [tolerance=±5% resistance=10k package=THT]
  R38 = Resistor [tolerance=±5% resistance=10k package=THT]
  R39 = Resistor [tolerance=±5% resistance=10k package=THT]
  R40 = Resistor [tolerance=±5% resistance=10k package=THT]
  R41 = Resistor [tolerance=±5% resistance=10k package=THT]
  R42 = Resistor [tolerance=±5% resistance=10k package=THT]
  R43 = Resistor [tolerance=±5% resistance=10k package=THT]
  R44 = Resistor [tolerance=±5% resistance=10k package=THT]
  R45 = Resistor [tolerance=±5% resistance=10k package=THT]
  R46 = Resistor [tolerance=±5% resistance=10k package=THT]
  R47 = Resistor [tolerance=±5% resistance=10k package=THT]
  R48 = Resistor [tolerance=±5% resistance=10k package=THT]
  R49 = Resistor [tolerance=±5% resistance=10k package=THT]
  R50 = Resistor [tolerance=±5% resistance=10k package=THT]
  R51 = Resistor [tolerance=±5% resistance=10k package=THT]
  R53 = Resistor [tolerance=±5% resistance=10k package=THT]
  R54 = Resistor [tolerance=±5% resistance=10k package=THT]
  R55 = Resistor [tolerance=±5% resistance=10k package=THT]
  R56 = Resistor [tolerance=±5% resistance=10k package=THT]
  R57 = Resistor [tolerance=±5% resistance=10k package=THT]
  C7 = Ceramic Capacitor [capacitance=100nF package="100 mil [THT, multilayer]"]
  U7 = 74HC165 [part_number=SN74LS165 package="DIP16 [THT]"]
  U8 = 74HC165 [part_number=SN74LS165 package="DIP16 [THT]"]
  U9 = 74HC165 [part_number=SN74LS165 package="DIP16 [THT]"]
  U10 = 74HC165 [part_number=SN74LS165 package="DIP16 [THT]"]
  U11 = 74HC165 [part_number=SN74LS165 package="DIP16 [THT]"]
  J15 = double row male pin header, 4 pins [form="♂ (male)"]
  J16 = double row male pin header, 4 pins [form="♂ (male)"]
  J17 = double row male pin header, 4 pins [form="♂ (male)"]
  J18 = double row male pin header, 4 pins [form="♂ (male)"]
  J20 = double row male pin header, 4 pins [form="♂ (male)"]
  J21 = double row male pin header, 4 pins [form="♂ (male)"]
  J22 = double row male pin header, 4 pins [form="♂ (male)"]
  J23 = double row male pin header, 4 pins [form="♂ (male)"]
  J24 = double row male pin header, 4 pins [form="♂ (male)"]
  J25 = double row male pin header, 4 pins [form="♂ (male)"]
  R60 = Resistor [tolerance=±5% resistance=10k package=THT]
  R61 = Resistor [tolerance=±5% resistance=10k package=THT]
  R62 = Resistor [tolerance=±5% resistance=10k package=THT]
  R63 = Resistor [tolerance=±5% resistance=10k package=THT]
  R65 = Resistor [tolerance=±5% resistance=10k package=THT]
  R67 = Resistor [tolerance=±5% resistance=10k package=THT]
  R68 = Resistor [tolerance=±5% resistance=10k package=THT]
  R70 = Resistor [tolerance=±5% resistance=10k package=THT]
  R71 = Resistor [tolerance=±5% resistance=10k package=THT]
  R72 = Resistor [tolerance=±5% resistance=10k package=THT]
  R73 = Resistor [tolerance=±5% resistance=10k package=THT]
  R75 = Resistor [tolerance=±5% resistance=10k package=THT]
  R76 = Resistor [tolerance=±5% resistance=10k package=THT]
  R77 = Resistor [tolerance=±5% resistance=10k package=THT]
  R78 = Resistor [tolerance=±5% resistance=10k package=THT]
  R79 = Resistor [tolerance=±5% resistance=10k package=THT]
  R80 = Resistor [tolerance=±5% resistance=10k package=THT]
  R81 = Resistor [tolerance=±5% resistance=10k package=THT]
  R82 = Resistor [tolerance=±5% resistance=10k package=THT]
  R83 = Resistor [tolerance=±5% resistance=10k package=THT]
  R85 = Resistor [tolerance=±5% resistance=10k package=THT]
  R86 = Resistor [tolerance=±5% resistance=10k package=THT]
  R87 = Resistor [tolerance=±5% resistance=10k package=THT]
  R89 = Resistor [tolerance=±5% resistance=10k package=THT]
  R90 = Resistor [tolerance=±5% resistance=10k package=THT]
  R91 = Resistor [tolerance=±5% resistance=10k package=THT]
  R92 = Resistor [tolerance=±5% resistance=10k package=THT]
  R93 = Resistor [tolerance=±5% resistance=10k package=THT]
  R94 = Resistor [tolerance=±5% resistance=10k package=THT]
  R95 = Resistor [tolerance=±5% resistance=10k package=THT]
  R96 = Resistor [tolerance=±5% resistance=10k package=THT]
  R97 = Resistor [tolerance=±5% resistance=10k package=THT]
  R98 = Resistor [tolerance=±5% resistance=10k package=THT]
  R99 = Resistor [tolerance=±5% resistance=10k package=THT]
  R100 = Resistor [tolerance=±5% resistance=10k package=THT]
  R101 = Resistor [tolerance=±5% resistance=10k package=THT]
  R102 = Resistor [tolerance=±5% resistance=10k package=THT]
  R104 = Resistor [tolerance=±5% resistance=10k package=THT]
  R105 = Resistor [tolerance=±5% resistance=10k package=THT]
  R106 = Resistor [tolerance=±5% resistance=10k package=THT]
  R107 = Resistor [tolerance=±5% resistance=10k package=THT]
  R108 = Resistor [tolerance=±5% resistance=10k package=THT]
  R110 = Resistor [tolerance=±5% resistance=10k package=THT]
  R111 = Resistor [tolerance=±5% resistance=10k package=THT]
  R112 = Resistor [tolerance=±5% resistance=10k package=THT]
  C8 = Ceramic Capacitor [capacitance=100nF package="100 mil [THT, multilayer]"]
  C9 = Ceramic Capacitor [capacitance=100nF package="100 mil [THT, multilayer]"]
  C10 = Ceramic Capacitor [capacitance=100nF package="100 mil [THT, multilayer]"]
  C12 = Ceramic Capacitor [capacitance=100nF package="100 mil [THT, multilayer]"]
  C13 = Ceramic Capacitor [capacitance=100nF package="100 mil [THT, multilayer]"]
  U12 = 74HC595 [package="DIP16 [THT]"]
  U13 = 74HC595 [package="DIP16 [THT]"]
  J26 = double row male pin header, 8 pins [form="♂ (male)"]
  J27 = double row male pin header, 8 pins [form="♂ (male)"]
  Power_plug1 = Power plug

nets (from the breadboard view):
  N1: U1.Q1, U2.Q1, U3.Q1, U4.Q1, U5.Q1, U6.Q1, Part1.D9_PWM
  N2: U1.Q2, U2.Q2, U3.Q2, U4.Q2, U5.Q2, U6.Q2, U12.SH_CP, U13.SH_CP
  N3: U1.Q3, J13.pin1, R2.Pin_0
  N4: U1.Q4, J13.pin2, R9.Pin_0
  N5: U1.Q5, J13.pin3, R10.Pin_0
  N6: U1.Q6, J13.pin4, R11.Pin_0
  N7: U1.Q7', Part1.D12/MISO
  N8: U1.MR, U2.Q7'
  N9: U1.SH_CP, J2.pin4, R12.Pin_1
  N10: U1.ST_CP, J2.pin3, R4.Pin_1
  N11: U1.OE, J2.pin2, R3.Pin_1
  N12: U1.DS, J2.pin1, R1.Pin_1
  N13: U1.Q0, U2.Q0, U3.Q0, U4.Q0, U5.Q0, U6.Q0, R6.Pin_1, R7.Pin_1, R25.Pin_1, R31.Pin_1, R45.Pin_1, R53.Pin_1, U7.Q0, U8.Q0, U9.Q0, U10.Q0, U11.Q0, R62.Pin_1, R71.Pin_1, R96.Pin_1, R106.Pin_1, R110.Pin_1
  N14: U2.Q3, J3.pin1, R16.Pin_0
  N15: U2.Q4, J3.pin2, R17.Pin_0
  N16: U2.Q5, J3.pin3, R18.Pin_0
  N17: U2.Q6, J3.pin4, R19.Pin_0
  N18: U2.MR, U3.Q7'
  N19: U2.SH_CP, J4.pin4, R15.Pin_1
  N20: U2.ST_CP, J4.pin3, R14.Pin_1
  N21: U2.OE, J4.pin2, R13.Pin_1
  N22: U2.DS, J4.pin1, R21.Pin_1
  N23: U3.Q3, J5.pin1, R20.Pin_0
  N24: U3.Q4, J5.pin2, R22.Pin_0
  N25: U3.Q5, J5.pin3, R23.Pin_0
  N26: U3.Q6, J5.pin4, R24.Pin_0
  N27: U3.MR, U4.Q7'
  N28: U3.SH_CP, J6.pin4, R29.Pin_1
  N29: U3.ST_CP, J6.pin3, R28.Pin_1
  N30: U3.OE, J6.pin2, R27.Pin_1
  N31: U3.DS, J6.pin1, R26.Pin_1
  N32: U4.Q3, J7.pin1, R35.Pin_0
  N33: U4.Q4, J7.pin2, R36.Pin_0
  N34: U4.Q5, J7.pin3, R37.Pin_0
  N35: U4.Q6, J7.pin4, R38.Pin_0
  N36: U4.MR, U5.Q7'
  N37: U4.SH_CP, J8.pin4, R30.Pin_1
  N38: U4.ST_CP, J8.pin3, R34.Pin_1
  N39: U4.OE, J8.pin2, R33.Pin_1
  N40: U4.DS, J8.pin1, R32.Pin_1
  N41: U5.Q3, J9.pin1, R41.Pin_0
  N42: U5.Q4, J9.pin2, R42.Pin_0
  N43: U5.Q5, J9.pin3, R43.Pin_0
  N44: U5.Q6, J9.pin4, R44.Pin_0
  N45: U5.MR, U6.Q7'
  N46: U5.SH_CP, J10.pin4, R48.Pin_1
  N47: U5.ST_CP, J10.pin3, R47.Pin_1
  N48: U5.OE, J10.pin2, R46.Pin_1
  N49: U5.DS, J10.pin1, R39.Pin_1
  N50: U6.Q3, J12.pin1, R49.Pin_0
  N51: U6.Q4, J12.pin2, R50.Pin_0
  N52: U6.Q5, J12.pin3, R40.Pin_0
  N53: U6.Q6, J12.pin4, R51.Pin_0
  N54: U6.SH_CP, J11.pin4, R57.Pin_1
  N55: U6.ST_CP, J11.pin3, R56.Pin_1
  N56: U6.OE, J11.pin2, R55.Pin_1
  N57: U6.DS, J11.pin1, R54.Pin_1
  N58: Part1.D10_PWM/SS, U12.ST_CP, U13.ST_CP
  N59: Part1.D11_PWM/MOSI, U12.DS
  VCC: Part1.5V, U12.MR, U12.VCC, U13.MR, U13.VCC
  GND: Part1.GND, U12.GND, U12.OE, U13.GND, U13.OE
  N60: R1.Pin_0, C1.1, C2.1, R2.Pin_1, R3.Pin_0, R4.Pin_0, R6.Pin_0, R7.Pin_0, R9.Pin_1, R10.Pin_1, R11.Pin_1, R12.Pin_0, R13.Pin_0, R14.Pin_0, R15.Pin_0, R16.Pin_1, R17.Pin_1, R18.Pin_1, R19.Pin_1, R20.Pin_1, R21.Pin_0, R22.Pin_1, R23.Pin_1, R24.Pin_1, R25.Pin_0, R26.Pin_0, R27.Pin_0, R28.Pin_0, R29.Pin_0, R30.Pin_0, C3.1, C4.1, C5.1, R31.Pin_0, R32.Pin_0, R33.Pin_0, R34.Pin_0, R35.Pin_1, R36.Pin_1, R37.Pin_1, R38.Pin_1, R39.Pin_0, R40.Pin_1, R41.Pin_1, R42.Pin_1, R43.Pin_1, R44.Pin_1, R45.Pin_0, R46.Pin_0, R47.Pin_0, R48.Pin_0, R49.Pin_1, R50.Pin_1, R51.Pin_1, R53.Pin_0, R54.Pin_0, R55.Pin_0, R56.Pin_0, R57.Pin_0, C7.1, R60.Pin_1, R61.Pin_0, R62.Pin_0, R63.Pin_0, R65.Pin_0, R67.Pin_1, R68.Pin_1, R70.Pin_1, R71.Pin_0, R72.Pin_1, R73.Pin_1, R75.Pin_1, R76.Pin_1, R77.Pin_0, R78.Pin_0, R79.Pin_1, R80.Pin_1, R81.Pin_0, R82.Pin_1, R83.Pin_1, R85.Pin_0, R86.Pin_0, R87.Pin_0, R89.Pin_0, R90.Pin_0, R91.Pin_1, R92.Pin_0, R93.Pin_1, R94.Pin_1, R95.Pin_0, R96.Pin_0, R97.Pin_1, R98.Pin_0, R99.Pin_0, R100.Pin_1, R101.Pin_0, R102.Pin_0, R104.Pin_1, R105.Pin_0, R106.Pin_0, R107.Pin_0, R108.Pin_1, R110.Pin_0, R111.Pin_1, R112.Pin_0, C8.1, C9.1, C10.1, C12.1, C13.1, Power_plug1.GND
  N61: C1.0, C2.0, C3.0, C4.0, C5.0, C7.0, C8.0, C9.0, C10.0, C12.0, C13.0, Power_plug1.VCC
  N62: U7.Q1, U8.Q1, U9.Q1, U10.Q1, U11.Q1
  N63: U7.Q2, U8.Q2, U9.Q2, U10.Q2, U11.Q2
  N64: U7.Q3, J23.pin1, R70.Pin_0
  N65: U7.Q4, J23.pin2, R82.Pin_0
  N66: U7.Q5, J23.pin3, R68.Pin_0
  N67: U7.Q6, J23.pin4, R100.Pin_0
  N68: U7.MR, U8.Q7'
  N69: U7.SH_CP, J16.pin4, R85.Pin_1
  N70: U7.ST_CP, J16.pin3, R90.Pin_1
  N71: U7.OE, J16.pin2, R95.Pin_1
  N72: U7.DS, J16.pin1, R101.Pin_1
  N73: U8.Q3, J17.pin1, R94.Pin_0
  N74: U8.Q4, J17.pin2, R67.Pin_0
  N75: U8.Q5, J17.pin3, R80.Pin_0
  N76: U8.Q6, J17.pin4, R76.Pin_0
  N77: U8.MR, U9.Q7'
  N78: U8.SH_CP, J21.pin4, R77.Pin_1
  N79: U8.ST_CP, J21.pin3, R63.Pin_1
  N80: U8.OE, J21.pin2, R78.Pin_1
  N81: U8.DS, J21.pin1, R81.Pin_1
  N82: U9.Q3, J18.pin1, R73.Pin_0
  N83: U9.Q4, J18.pin2, R72.Pin_0
  N84: U9.Q5, J18.pin3, R97.Pin_0
  N85: U9.Q6, J18.pin4, R60.Pin_0
  N86: U9.MR, U10.Q7'
  N87: U9.SH_CP, J15.pin4, R61.Pin_1
  N88: U9.ST_CP, J15.pin3, R105.Pin_1
  N89: U9.OE, J15.pin2, R65.Pin_1
  N90: U9.DS, J15.pin1, R102.Pin_1
  N91: U10.Q3, J22.pin1, R83.Pin_0
  N92: U10.Q4, J22.pin2, R75.Pin_0
  N93: U10.Q5, J22.pin3, R111.Pin_0
  N94: U10.Q6, J22.pin4, R91.Pin_0
  N95: U10.MR, U11.Q7'
  N96: U10.SH_CP, J20.pin4, R99.Pin_1
  N97: U10.ST_CP, J20.pin3, R86.Pin_1
  N98: U10.OE, J20.pin2, R87.Pin_1
  N99: U10.DS, J20.pin1, R112.Pin_1
  N100: U11.Q3, J25.pin1, R79.Pin_0
  N101: U11.Q4, J25.pin2, R93.Pin_0
  N102: U11.Q5, J25.pin3, R104.Pin_0
  N103: U11.Q6, J25.pin4, R108.Pin_0
  N104: U11.SH_CP, J24.pin4, R98.Pin_1
  N105: U11.ST_CP, J24.pin3, R89.Pin_1
  N106: U11.OE, J24.pin2, R107.Pin_1
  N107: U11.DS, J24.pin1, R92.Pin_1
  N108: U12.Q1, J26.pin2
  N109: U12.Q2, J26.pin3
  N110: U12.Q3, J26.pin4
  N111: U12.Q4, J26.pin5
  N112: U12.Q5, J26.pin6
  N113: U12.Q6, U12.Q7, J26.pin7, J26.pin8
  N114: U12.Q7', U13.DS
  N115: U12.Q0, J26.pin1
  N116: U13.Q1, J27.pin2
  N117: U13.Q2, J27.pin3
  N118: U13.Q3, J27.pin4
  N119: U13.Q4, J27.pin5
  N120: U13.Q5, J27.pin6
  N121: U13.Q6, J27.pin7
  N122: U13.Q7, J27.pin8
  N123: U13.Q0, J27.pin1

custom parts:
  74HC165: 8-bit parallel-load shift registers
